# Fritzing sketch simon_sketch (saved by Fritzing 0.9.2b)
circuit board: 8.46667cm x 5.64444cm
breadboards: 1

parts:
  Part1 = Arduino Uno (Rev3)
  LED2 = LED - 5mm [color="Red (633nm)" package="5 mm [THT]"]
  LED4 = LED - 5mm [color="Blue (470nm)" package="5 mm [THT]"]
  LED1 = LED - 5mm [color="Yellow (585nm)" package="5 mm [THT]"]
  LED3 = LED - 5mm [color="Green (560nm)" package="5 mm [THT]"]
  R3 = Resistor [tolerance=±5% resistance=220 package="2010 [SMD]"]
  R4 = Resistor [tolerance=±5% resistance=220 package="2010 [SMD]"]
  R2 = Resistor [tolerance=±5% resistance=220 package="2010 [SMD]"]
  S2 = Pushbutton [package="[THT]"]
  S1 = Pushbutton [package="[THT]"]
  S3 = Pushbutton [package="[THT]"]
  S4 = Pushbutton [package="[THT]"]
  R1 = Resistor [tolerance=±5% resistance=220 package="2010 [SMD]"]

nets (from the schematic view):
  N1: Part1.D8, R1.Pin_1
  N2: Part1.D9_PWM, Part1.D7, S3.Pin_3, S3.Pin_4
  N3: Part1.D10_PWM/SS, R3.Pin_1
  N4: Part1.D12/MISO, R4.Pin_1
  N5: Part1.GND, S1.Pin_1, S1.Pin_2
  N6: Part1.D6_PWM, R2.Pin_1
  N7: Part1.5V, LED2.cathode, LED1.cathode, S4.Pin_3, S4.Pin_4
  N8: LED2.anode, R2.Pin_0
  N9: LED4.anode, R4.Pin_0
  N10: LED1.anode, R1.Pin_0
  N11: LED3.anode, R3.Pin_0
  N12: S2.Pin_1, S2.Pin_2
  N13: S2.Pin_3, S2.Pin_4
  N14: S1.Pin_3, S1.Pin_4
  N15: S3.Pin_1, S3.Pin_2
  N16: S4.Pin_1, S4.Pin_2
